// Logisim project ex1.circ as structural Verilog: 5 circuits, main circuit NAND1
module NAND1 (
  input  A,
  input  B,
  output RESULT
);

  wire and_1_out;

  and and_1 (and_1_out, A, B);
  not not_1 (RESULT, and_1_out);

  // Notes on the sheet:
  //   PUT CIRCUITRY HERE
endmodule

module NOR1 (
  input  A,
  input  B,
  output RESULT
);

  wire or_1_out;

  or or_1 (or_1_out, A, B);
  not not_1 (RESULT, or_1_out);

  // Notes on the sheet:
  //   PUT CIRCUITRY HERE
endmodule

module XOR1 (
  input  A,
  input  B,
  output RESULT
);

  wire nand1_1_result, or_1_out;

  or or_1 (or_1_out, A, B);
  NAND1 nand1_1 (.A(A), .B(B), .RESULT(nand1_1_result));
  and and_1 (RESULT, nand1_1_result, or_1_out);

  // Notes on the sheet:
  //   PUT CIRCUITRY HERE
endmodule

module MUX2 (
  input  B,
  input  A,
  input  Sel,
  output RESULT
);

  wire and_1_out, and_2_out, not_1_out;

  not not_1 (not_1_out, Sel);
  and and_1 (and_1_out, B, Sel);
  and and_2 (and_2_out, A, not_1_out);
  or or_1 (RESULT, and_1_out, and_2_out);

  // Notes on the sheet:
  //   PUT CIRCUITRY HERE
endmodule

module MUX4 (
  input  D,
  input  C,
  input  B,
  input  A,
  input  Sel1,
  input  Sel2,
  output RESULT
);

  wire and_1_out, and_2_out, and_3_out, and_4_out, not_1_out, not_2_out;

  not not_1 (not_1_out, Sel1);
  not not_2 (not_2_out, Sel2);
  and and_1 (and_1_out, D, Sel1, Sel2);
  and and_2 (and_2_out, C, Sel1, not_2_out);
  and and_3 (and_3_out, B, Sel2, not_1_out);
  and and_4 (and_4_out, A, not_1_out, not_2_out);
  or or_1 (RESULT, and_1_out, and_2_out, and_3_out, and_4_out);

  // Notes on the sheet:
  //   PUT CIRCUITRY HERE
endmodule
